# Fritzing sketch Untitled Sketch 2 (saved by Fritzing 1.0.1rc)
breadboards: 1

parts:
  Part1 = Arduino Uno (Rev3)
  LED1 = LEDs [package=led10mm]
  LED2 = LEDs [package=led10mm]
  LED3 = LEDs [package=led10mm]
  S1 = Pushbutton [package="[THT]"]
  R1 = Resistor [tolerance=±5% resistance=220 package="2010 [SMD]"]
  R2 = Resistor [tolerance=±5% resistance=220 package="2010 [SMD]"]
  R3 = Resistor [tolerance=±5% resistance=220 package="2010 [SMD]"]
  R4 = Resistor [tolerance=±5% resistance=220 package="2010 [SMD]"]

nets:
  N1: Part1.D9_PWM, R3.Pin_0
  N2: Part1.D10_PWM/SS, R1.Pin_0
  N3: Part1.D11_PWM/MOSI, R2.Pin_0
  N4: Part1.D12/MISO, R4.Pin_0
  N5: Part1.GND, LED1.A, LED2.A, LED3.A, S1.Pin_1, S1.Pin_2
  N6: LED1.C, R1.Pin_1
  N7: LED2.C, R2.Pin_1
  N8: LED3.C, R3.Pin_1
  N9: S1.Pin_3, S1.Pin_4, R4.Pin_1
